# Fritzing sketch schema (saved by Fritzing 0.9.3b)

parts:
  WeMos_D1_Mini1 = WeMos D1 Mini
  Součástka1 = Adafruit SHT31-D Sensirion Temperature/Humidity Sensor [part_number="Adafruit #2857"]
  IC1 = Voltage Regulator [package=to-92]
  U1 = LIPO-110mAh [package=lipo-110]
  S1 = Reed switch [package=THT]
  S2 = Reed switch [package=THT]

nets:
  3V3: WeMos_D1_Mini1.3V3, Součástka1.VIN, IC1.OUT, S1.pin_1, S2.pin_1
  N1: WeMos_D1_Mini1.D1, Součástka1.SCL
  N2: WeMos_D1_Mini1.D2, Součástka1.SDA
  N3: WeMos_D1_Mini1.D5, S2.pin_2
  N4: WeMos_D1_Mini1.D6, S1.pin_2
  N5: WeMos_D1_Mini1.G, Součástka1.GND
  N6: IC1.GND, U1.-
  N7: IC1.IN, U1.+

notes:
  5V -> 3.3V
  Magnetick lockers

custom parts:
  Adafruit SHT31-D Sensirion Temperature/Humidity Sensor: Sensirion Temperature/Humidity sensors are some of the finest & highest-accuracy devices you can get. And, finally we have some that have a true I2C interface for easy reading. The SHT31-D sensor has an excellent ±2% relative humidity and ±0.3°C accuracy for most uses. Unlike earlier SHT sensors, this sensor has a true I2C interface, and (bonus!) even with two address options. It also is 3V or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
